// Digital circuit Casa_Automatica.dig as structural Verilog
module Casa_Automatica (
  input  Modo_Seguro,
  input  Janela_1,
  input  Janela_2,
  input  Janela_3,
  input  Porta,
  input  Porta_Trancada,
  input  Sensor_Crepuscular,
  input  Sensor_de_chuva,
  input  Temperatura_abixo_de_15,
  input  Caixa_B_cheia,
  input  [3:0] Sensor_de_A,
  input  Ligar_Bomba
);

  wire not_1_out, u_Caixas_de_Agua_cab, u_Caixas_de_Agua_eva, u_decod_out1, u_decod_out2, u_decod_out3,
       u_decod_out4, u_decod_out5;
  wire [4:0] u_alerta_alt;

  not not_1 (not_1_out, Porta_Trancada);
  alerta #(.applicationType("GHDL"), .CodeFile("/home/aluno/Documentos/VHDL/Casa_Automática/CasaAutomatica_Alerta.vhdl")) u_alerta (
    .MS(Modo_Seguro), .J1(Janela_1), .J2(Janela_2), .J3(Janela_3), .P(Porta), .PT(not_1_out),
    .SC(Sensor_Crepuscular), .SCh(Sensor_de_chuva), .T(Temperatura_abixo_de_15), .ALT(u_alerta_alt));
  Caixas_de_Agua #(.applicationType("GHDL"), .CodeFile("/home/aluno/Documentos/VHDL/Casa_Automática/CasaAutomatica_Caixas.vhdl")) u_Caixas_de_Agua (
    .SA(Sensor_de_A), .SB(Caixa_B_cheia), .Bomba_Ligada(Ligar_Bomba), .CAB(u_Caixas_de_Agua_cab),
    .EVA(u_Caixas_de_Agua_eva));
  decod #(.applicationType("GHDL"), .CodeFile("/home/aluno/Documentos/VHDL/Casa_Automática(T1)/Decod.vhdl")) u_decod (
    .entrada(u_alerta_alt), .out1(u_decod_out1), .out2(u_decod_out2), .out3(u_decod_out3),
    .out4(u_decod_out4), .out5(u_decod_out5));
  LED \Caixa_A_está_bombeando_para_B  (.in(u_Caixas_de_Agua_cab));
  LED \Eletroválvula_de_A_está_ligada  (.in(u_Caixas_de_Agua_eva));
  LED Modo_seguro_e_janelas_abertas (.in(u_decod_out1));
  LED Porta_aberta_mas_trancada (.in(u_decod_out2));
  LED Chovendo_e_portas_ou_janelas_abertas (.in(u_decod_out3));
  LED Noite_e_janelas_abertas (.in(u_decod_out4));
  LED Temperatura_baixa__ejanelas_abertas (.in(u_decod_out5));

  // Notes on the sheet:
  //   Não consegui usar os inteiros, a média não era calculada certa
  //   Explicação dos casos de teste:
  //   1º ao 3º = Alerta ativado se alguma janela estiver aberta com o modo seguro ativado;
  //   4º = Alerta ativado se porta estiver aberta mas trancada;
  //   5º = Alerta desativado se o modo seguro estiver ligado, a porta aberta mas destrancada;
  //   6º = Alerta desativado se todas janelas e a porta estiverem aberta mas o modo seguro desativado;
  //   6º = Alerta ativado se a porta estiver aberta mas trancada;
  //   7º ao 9º = Alerta ativado se estiver chovendo e alguma porta ou janela estiver aberta;
  //   10º = Alarme desativado se for a noite e a porta estiver aberta mas destrancada;
  //   11º ao 13º = Alarme ativado se for a noite e alguma das janelas estiver aberta;
  //   14º ao 16º = Alarme ativado se a temperatura estiver baixa e alguma janela estiver aberta;
  //   17º = Alarme desativado se a temperatura estiver baixa mas apenas a porta estiver aberta;
endmodule

/* Test case:
Modo_Seguro Janela_1 Janela_2 Janela_3 Porta Porta_Trancada Sensor_Crepuscular Sensor_de_chuva Temperatura_abixo_de_15 Modo_seguro_e_janelas_abertas Porta_aberta_mas_trancada Chovendo_e_portas_ou_janelas_abertas Noite_e_janelas_abertas Temperatura_baixa__ejanelas_abertas
1 1 0 0 0 0 0 0 0 1 0 0 0 0
1 0 1 0 0 0 0 0 0 1 0 0 0 0
1 0 0 1 0 0 0 0 0 1 0 0 0 0
1 0 0 0 1 1 0 0 0 0 1 0 0 0
1 0 0 0 1 0 0 0 0 0 0 0 0 0
0 1 1 1 1 0 0 0 0 0 0 0 0 0
0 0 0 0 1 0 0 1 0 0 0 1 0 0
0 0 0 1 0 0 0 1 0 0 0 1 0 0
0 1 0 0 0 0 0 1 0 0 0 1 0 0
0 0 0 0 1 0 1 0 0 0 0 0 0 0
0 0 0 1 0 0 1 0 0 0 0 0 1 0
0 0 1 0 0 0 1 0 0 0 0 0 1 0
0 1 0 0 0 0 1 0 0 0 0 0 1 0
0 0 0 1 0 0 0 0 1 0 0 0 0 1
0 0 1 0 0 0 0 0 1 0 0 0 0 1
0 1 0 0 0 0 0 0 1 0 0 0 0 1
0 0 0 0 1 0 0 0 1 0 0 0 0 0
*/
