// Digital circuit Ex1.dig as structural Verilog
module Ex1 (
  input  A,
  input  B,
  input  C,
  input  D,
  output S
);

  ou #(.applicationType("GHDL"), .CodeFile("/home/aluno/Documentos/VHDL/Ex1.vhdl")) u_ou (
    .a(A), .b(B), .c(C), .d(D), .s(S));
endmodule

/* Test case:
A B C D S
1 1 0 0 1
0 1 0 0 1
0 0 1 0 1
0 0 0 1 1
0 0 0 0 0
*/
