// Digital circuit Casa_Automatica.dig as structural Verilog
module Casa_Automatica (
  input  Caixa_B_cheia,
  input  [3:0] Sensor_de_A,
  input  Ligar_Bomba,
  input  in_4,
  input  in_5,
  input  in_6
);

  wire u_alerta_alt1, u_alerta_alt2, u_Caixas_de_Agua_cab, u_Caixas_de_Agua_eva;

  alerta #(.applicationType("GHDL"), .CodeFile("/home/aluno/Documentos/Casa_Automática(T1)/CasaAutomatica_Alerta.vhdl")) u_alerta (
    .MS(in_6), .J1(in_4), .P(in_5), .ALT1(u_alerta_alt1), .ALT2(u_alerta_alt2));
  Caixas_de_Agua #(.applicationType("GHDL"), .CodeFile("/home/aluno/Documentos/VHDL/Casa_Automática/CasaAutomatica_Caixas.vhdl")) u_Caixas_de_Agua (
    .SA(Sensor_de_A), .SB(Caixa_B_cheia), .Bomba_Ligada(Ligar_Bomba), .CAB(u_Caixas_de_Agua_cab),
    .EVA(u_Caixas_de_Agua_eva));
  LED led_1 (.in(u_alerta_alt1));
  LED led_2 (.in(u_alerta_alt2));
  LED \Caixa_A_está_bombeando_para_B  (.in(u_Caixas_de_Agua_cab));
  LED \Eletroválvula_de_A_está_ligada  (.in(u_Caixas_de_Agua_eva));
endmodule
