// Digital circuit Contador_Gray.dig as structural Verilog
module Contador_Gray (
  input  clk,
  output out_1,
  output out_2,
  output out_3,
  output out_4
);

  wire and_1_out, and_2_out, and_3_out, and_4_out, and_5_out, and_6_out, and_7_out, and_8_out, and_9_out,
       and_10_out, Clear_out, jk_ff_as_1_nq, jk_ff_as_2_nq, jk_ff_as_3_nq, jk_ff_as_4_nq, or_1_out, or_2_out,
       or_3_out, or_4_out, xor_1_out, xor_2_out;

  and and_1 (and_1_out, out_1, out_2, out_3);
  or or_1 (or_1_out, xor_1_out, and_1_out);
  xor xor_1 (xor_1_out, out_1, out_3, out_2);
  and and_2 (and_2_out, jk_ff_as_2_nq, jk_ff_as_4_nq, jk_ff_as_3_nq);
  or or_2 (or_2_out, xor_2_out, and_2_out);
  Button Clear (.out(Clear_out));
  xor xor_2 (xor_2_out, jk_ff_as_2_nq, jk_ff_as_3_nq, jk_ff_as_4_nq);
  and and_3 (and_3_out, out_4, out_1, jk_ff_as_3_nq);
  and and_4 (and_4_out, out_4, out_2, jk_ff_as_4_nq);
  or or_3 (or_3_out, and_4_out, and_3_out);
  JK_FF_AS jk_ff_as_1 (.Set(1'b0), .J(or_2_out), .C(clk), .K(or_1_out), .Clr(Clear_out), .Q(out_4), .nQ(jk_ff_as_1_nq));
  and and_5 (and_5_out, out_4, out_1, out_2);
  and and_6 (and_6_out, out_4, jk_ff_as_4_nq, jk_ff_as_3_nq);
  or or_4 (or_4_out, and_6_out, and_5_out);
  and and_7 (and_7_out, out_1, jk_ff_as_1_nq, out_3);
  and and_8 (and_8_out, jk_ff_as_4_nq, jk_ff_as_1_nq, out_3);
  JK_FF_AS jk_ff_as_2 (.Set(1'b0), .J(or_4_out), .C(clk), .K(or_3_out), .Clr(Clear_out), .Q(out_3), .nQ(jk_ff_as_2_nq));
  JK_FF_AS jk_ff_as_3 (
    .Set(1'b0), .J(and_8_out), .C(clk), .K(and_7_out), .Clr(Clear_out), .Q(out_2), .nQ(jk_ff_as_3_nq));
  and and_9 (and_9_out, out_2, jk_ff_as_2_nq, jk_ff_as_1_nq);
  and and_10 (and_10_out, jk_ff_as_2_nq, jk_ff_as_3_nq, jk_ff_as_1_nq);
  JK_FF_AS jk_ff_as_4 (
    .Set(1'b0), .J(and_9_out), .C(clk), .K(and_10_out), .Clr(Clear_out), .Q(out_1), .nQ(jk_ff_as_4_nq));

  // Notes on the sheet:
  //   JK0
  //   JK1
  //   JK2
  //   JK3
endmodule
