// Digital circuit ex1.dig as structural Verilog
module ex1 (
  input  [2:0] in_1
);

  wire [7:0] u_decoder_3to8_y;

  decoder_3to8 #(.applicationType("GHDL"), .CodeFile("C:\\Users\\Pichau\\Documents\\C0de\\UFFS\\Sistemas\\Sistemas_2\\Exercicios\\ex1.vhd")) u_decoder_3to8 (
    .A(in_1), .Y(u_decoder_3to8_y));
  LED led_1 (.in(u_decoder_3to8_y[0]));
  LED led_2 (.in(u_decoder_3to8_y[1]));
  LED led_3 (.in(u_decoder_3to8_y[2]));
  LED led_4 (.in(u_decoder_3to8_y[3]));
  LED led_5 (.in(u_decoder_3to8_y[4]));
  LED led_6 (.in(u_decoder_3to8_y[5]));
  LED led_7 (.in(u_decoder_3to8_y[6]));
  LED led_8 (.in(u_decoder_3to8_y[7]));
endmodule
