// Digital circuit ex2.dig as structural Verilog
module ex2 (
  input  [1:0] in_1,
  input  in_2
);

  wire [3:0] u_decoder_2to4en_y_l;

  decoder_2to4en #(.applicationType("GHDL"), .CodeFile("C:\\Users\\Pichau\\Documents\\C0de\\UFFS\\Sistemas\\Sistemas_2\\Exercicios\\ex2.vhd")) u_decoder_2to4en (
    .EN(in_2), .A(in_1), .Y_L(u_decoder_2to4en_y_l));
  LED led_1 (.in(u_decoder_2to4en_y_l[0]));
  LED led_2 (.in(u_decoder_2to4en_y_l[1]));
  LED led_3 (.in(u_decoder_2to4en_y_l[2]));
  LED led_4 (.in(u_decoder_2to4en_y_l[3]));
endmodule
