// Digital circuit ex3.dig as structural Verilog
module ex3 (
  input  in_1,
  input  [3:0] in_2
);

  wire [6:0] u_bcd7seg_s;

  bcd7seg #(.applicationType("GHDL"), .CodeFile("C:\\Users\\Pichau\\Documents\\C0de\\UFFS\\Sistemas\\Sistemas_2\\Exercicios\\ex3.vhd")) u_bcd7seg (
    .EN(in_1), .D(in_2), .S(u_bcd7seg_s));
  Seven_Seg seven_seg_1 (
    .a(u_bcd7seg_s[6]), .b(u_bcd7seg_s[5]), .c(u_bcd7seg_s[4]), .d(u_bcd7seg_s[3]), .e(u_bcd7seg_s[2]),
    .f(u_bcd7seg_s[1]), .g(u_bcd7seg_s[0]), .dp(1'b0));
endmodule
