// Digital circuit ex4.dig as structural Verilog
module ex4 (
  input  [3:0] in_1,
  input  [3:0] in_2,
  input  [3:0] in_3,
  input  [3:0] in_4,
  input  [1:0] in_5,
  output [3:0] out_6
);

  mux #(.applicationType("GHDL"), .CodeFile("C:\\Users\\Softex\\Documents\\UFFS\\Sistemas\\Sistemas_2\\Exercicios\\ex4.vhd")) u_mux (
    .I0(in_1), .I1(in_2), .I2(in_3), .I3(in_4), .SEL(in_5), .Y(out_6));
endmodule
