// Digital circuit ex5.dig as structural Verilog
module ex5 (
  input  [15:0] in_1,
  input  [15:0] in_2,
  input  [15:0] in_3,
  input  [15:0] in_4,
  input  [15:0] in_5,
  input  [15:0] in_6,
  input  [15:0] in_7,
  input  [15:0] in_8,
  input  [2:0] in_9,
  output [15:0] out_10
);

  demux #(.applicationType("GHDL"), .CodeFile("C:\\Users\\Softex\\Documents\\UFFS\\Sistemas\\Sistemas_2\\Exercicios\\ex5.vhd")) u_demux (
    .I0(in_1), .I1(in_2), .I2(in_3), .I3(in_4), .I4(in_5), .I5(in_6), .I6(in_7), .I7(in_8), .SEL(in_9),
    .NUM(out_10));
endmodule
