// Digital circuit ex6.dig as structural Verilog
module ex6 (
  input  in_1,
  output [3:0] out_2
);

  wire button_1_out, button_2_out, u_counterr_ov;

  Button button_1 (.out(button_1_out));
  Button button_2 (.out(button_2_out));
  counterr #(.applicationType("GHDL"), .CodeFile("C:\\Users\\Pichau\\Documents\\C0de\\UFFS\\Sistemas\\Sistemas_2\\Exercicios\\ex6.vhd")) u_counterr (
    .enable(in_1), .clock(button_1_out), .reset(button_2_out), .count(out_2), .ov(u_counterr_ov));
  LED led_1 (.in(u_counterr_ov));
endmodule
