// Digital circuit Som_3bits.dig as structural Verilog
module Som_3bits (
  input  [2:0] in_1,
  input  [2:0] in_2,
  output [2:0] out_3
);

  wire u_adder3bits_overflow;

  adder3bits #(.applicationType("GHDL"), .CodeFile("C:\\Users\\Softex\\Documents\\UFFS\\Sistemas\\Sistemas_2\\Somd_3bits.vhd")) u_adder3bits (
    .a_f3(in_1), .b_f3(in_2), .overflow(u_adder3bits_overflow), .sum(out_3));
  LED led_1 (.in(u_adder3bits_overflow));
endmodule
