// Digital circuit blackJack_unificado.dig as structural Verilog
module blackJack_unificado (
  input  \Cartas_Alatórias ,
  input  Start,
  input  Hit,
  input  Stay,
  input  [3:0] \Próxima_carta 
);

  wire [1:0] Reset_out;
  wire [6:0] not_1_out, not_2_out, not_3_out, not_4_out, u_blackJack_hex0, u_blackJack_hex1,
       u_blackJack_hex2, u_blackJack_hex3, u_blackJack_ledg;
  wire [9:0] u_blackJack_ledr;

  Button Clock (.out(Reset_out[1]));
  Button Reset (.out(Reset_out[0]));
  blackJack #(.applicationType("GHDL"), .CodeFile("C:\\Users\\Pichau\\Documents\\C0de\\UFFS\\Sistemas\\Sistemas_2\\TF\\Digital\\blackJack_digital.vhd")) u_blackJack (
    .sw({\Próxima_carta , 2'b00, Stay, Hit, Start, \Cartas_Alatórias }), .key({2'b00, Reset_out}),
    .ledr(u_blackJack_ledr), .ledg(u_blackJack_ledg), .hex0(u_blackJack_hex0), .hex1(u_blackJack_hex1),
    .hex2(u_blackJack_hex2), .hex3(u_blackJack_hex3));
  Seven_Seg seven_seg_1 (
    .a(not_1_out[0]), .b(not_1_out[1]), .c(not_1_out[2]), .d(not_1_out[3]), .e(not_1_out[4]),
    .f(not_1_out[5]), .g(not_1_out[6]), .dp(1'b0));
  assign not_1_out = ~u_blackJack_hex3;  // Not not_1, 7 bits wide
  Seven_Seg seven_seg_2 (
    .a(not_2_out[0]), .b(not_2_out[1]), .c(not_2_out[2]), .d(not_2_out[3]), .e(not_2_out[4]),
    .f(not_2_out[5]), .g(not_2_out[6]), .dp(1'b0));
  LED led_1 (.in(u_blackJack_ledg[6]));
  assign not_2_out = ~u_blackJack_hex2;  // Not not_2, 7 bits wide
  assign not_3_out = ~u_blackJack_hex1;  // Not not_3, 7 bits wide
  LED led_2 (.in(u_blackJack_ledr[0]));
  Seven_Seg seven_seg_3 (
    .a(not_3_out[0]), .b(not_3_out[1]), .c(not_3_out[2]), .d(not_3_out[3]), .e(not_3_out[4]),
    .f(not_3_out[5]), .g(not_3_out[6]), .dp(1'b0));
  assign not_4_out = ~u_blackJack_hex0;  // Not not_4, 7 bits wide
  Seven_Seg seven_seg_4 (
    .a(not_4_out[0]), .b(not_4_out[1]), .c(not_4_out[2]), .d(not_4_out[3]), .e(not_4_out[4]),
    .f(not_4_out[5]), .g(not_4_out[6]), .dp(1'b0));
endmodule
