// Digital circuit dealer.dig as structural Verilog
module dealer (
  input  [3:0] in_1,
  input  in_3,
  output [4:0] out_2
);

  wire button_1_out, button_2_out, u_dealer_getcard, u_dealer_over;

  Button button_1 (.out(button_1_out));
  Button button_2 (.out(button_2_out));
  dealer #(.applicationType("GHDL"), .CodeFile("C:\\Users\\Softex\\Documents\\UFFS\\Sistemas\\Sistemas_2\\TF\\dealer.vhd")) u_dealer (
    .start(in_3), .clock(button_2_out), .reset(button_1_out), .nextCard(in_1), .getCard(u_dealer_getcard),
    .currentV(out_2), .over(u_dealer_over));
  LED led_1 (.in(u_dealer_getcard));
  LED led_2 (.in(u_dealer_over));
endmodule
