// Digital circuit player.dig as structural Verilog
module player (
  input  [3:0] in_1,
  input  in_3,
  input  in_4,
  input  in_5,
  output [4:0] out_2
);

  wire button_1_out, button_2_out, u_player_getcard, u_player_over;

  Button button_1 (.out(button_1_out));
  Button button_2 (.out(button_2_out));
  player #(.applicationType("GHDL"), .CodeFile("C:\\Users\\Pichau\\Documents\\C0de\\UFFS\\Sistemas\\Sistemas_2\\TF\\player.vhd")) u_player (
    .Hit(in_4), .start(in_3), .clock(button_2_out), .reset(button_1_out), .stay(in_5), .nextCard(in_1),
    .getCard(u_player_getcard), .currentV(out_2), .over(u_player_over));
  LED led_1 (.in(u_player_getcard));
  LED led_2 (.in(u_player_over));
endmodule
