// Digital circuit pontuacao.dig as structural Verilog
module pontuacao (
  input  in_1,
  input  [3:0] in_2,
  input  in_3,
  input  in_4,
  input  \Cartas_Aleatórias ,
  output [4:0] out_5,
  output [3:0] out_7
);

  wire button_1_out, button_2_out, or_1_out, u_dealer_getcard, u_dealer_over, u_player_getcard,
       u_player_over, u_pontuacao_startdealer;
  wire [1:0] u_pontuacao_result;
  wire [3:0] multiplexer_1_out;
  wire [4:0] u_dealer_currentv, u_player_currentv;
  wire [6:0] not_1_out, not_2_out, not_3_out, not_4_out, u_saida_hex0, u_saida_hex1, u_saida_hex2,
       u_saida_hex3, u_saida_ledg;
  wire [9:0] u_saida_ledr;

  random_generator #(.applicationType("GHDL"), .CodeFile("C:\\Users\\Softex\\Documents\\UFFS\\Sistemas\\Sistemas_2\\TF\\cards.vhdl")) u_random_generator (
    .clk(or_1_out), .reset(1'b0), .enable(1'b1), .random_number(out_7));
  Multiplexer #(.Bits(4)) multiplexer_1 (.sel(\Cartas_Aleatórias ), .in_0(in_2), .in_1(out_7), .out(multiplexer_1_out));
  Button button_1 (.out(button_1_out));
  Button button_2 (.out(button_2_out));
  dealer #(.applicationType("GHDL"), .CodeFile("C:\\Users\\Softex\\Documents\\UFFS\\Sistemas\\Sistemas_2\\TF\\dealer.vhd")) u_dealer (
    .start(u_pontuacao_startdealer), .clock(button_1_out), .reset(button_2_out),
    .nextCard(multiplexer_1_out), .getCard(u_dealer_getcard), .currentV(u_dealer_currentv),
    .over(u_dealer_over));
  player #(.applicationType("GHDL"), .CodeFile("C:\\Users\\Softex\\Documents\\UFFS\\Sistemas\\Sistemas_2\\TF\\player.vhd")) u_player (
    .Hit(in_3), .start(in_1), .clock(button_1_out), .reset(button_2_out), .stay(in_4),
    .nextCard(multiplexer_1_out), .getCard(u_player_getcard), .currentV(u_player_currentv),
    .over(u_player_over));
  LED led_1 (.in(u_dealer_getcard));
  LED led_2 (.in(u_player_getcard));
  or or_1 (or_1_out, u_dealer_getcard, u_player_getcard);
  pontuacao #(.applicationType("GHDL"), .CodeFile("C:\\Users\\Softex\\Documents\\UFFS\\Sistemas\\Sistemas_2\\TF\\pontuacao.vhd")) u_pontuacao (
    .Stay_Player(u_player_over), .points_player(u_player_currentv), .stay_dealer(u_dealer_over),
    .points_dealer(u_dealer_currentv), .reset(button_2_out), .clock(button_1_out),
    .startDealer(u_pontuacao_startdealer), .result(u_pontuacao_result), .pointsShown(out_5));
  Seven_Seg seven_seg_1 (
    .a(not_1_out[0]), .b(not_1_out[1]), .c(not_1_out[2]), .d(not_1_out[3]), .e(not_1_out[4]),
    .f(not_1_out[5]), .g(not_1_out[6]), .dp(1'b0));
  saida #(.applicationType("GHDL"), .CodeFile("C:\\Users\\Softex\\Documents\\UFFS\\Sistemas\\Sistemas_2\\TF\\saida.vhd")) u_saida (
    .last_card(multiplexer_1_out), .result(u_pontuacao_result), .pointsShown(out_5), .cardRequest(or_1_out),
    .HEX0(u_saida_hex0), .HEX1(u_saida_hex1), .HEX2(u_saida_hex2), .HEX3(u_saida_hex3), .ledg(u_saida_ledg),
    .ledr(u_saida_ledr));
  assign not_1_out = ~u_saida_hex3;  // Not not_1, 7 bits wide
  Seven_Seg seven_seg_2 (
    .a(not_2_out[0]), .b(not_2_out[1]), .c(not_2_out[2]), .d(not_2_out[3]), .e(not_2_out[4]),
    .f(not_2_out[5]), .g(not_2_out[6]), .dp(1'b0));
  assign not_2_out = ~u_saida_hex2;  // Not not_2, 7 bits wide
  LED led_3 (.in(u_saida_ledg[6]));
  Seven_Seg seven_seg_3 (
    .a(not_3_out[0]), .b(not_3_out[1]), .c(not_3_out[2]), .d(not_3_out[3]), .e(not_3_out[4]),
    .f(not_3_out[5]), .g(not_3_out[6]), .dp(1'b0));
  assign not_3_out = ~u_saida_hex1;  // Not not_3, 7 bits wide
  LED led_4 (.in(u_saida_ledr[0]));
  assign not_4_out = ~u_saida_hex0;  // Not not_4, 7 bits wide
  Seven_Seg seven_seg_4 (
    .a(not_4_out[0]), .b(not_4_out[1]), .c(not_4_out[2]), .d(not_4_out[3]), .e(not_4_out[4]),
    .f(not_4_out[5]), .g(not_4_out[6]), .dp(1'b0));
endmodule
