// Digital circuit portao.dig as structural Verilog
module portao (
  input  Sensor_de_erro,
  input  \Botão 
);

  wire [3:1] Reset_out;
  wire [6:0] not_1_out, u_portao_hex0;
  wire [9:0] u_portao_ledr;

  Button Reset (.out(Reset_out[1]));
  portao #(.applicationType("GHDL"), .CodeFile("C:\\Users\\Pichau\\Documents\\C0de\\UFFS\\Sistemas\\Sistemas_2\\portao\\Digital\\portao.vhd")) u_portao (
    .sw({{9{1'b0}}, Sensor_de_erro}), .key({Reset_out[3], 1'b0, Reset_out[1], \Botão }),
    .ledr(u_portao_ledr), .hex0(u_portao_hex0));
  Button Clock (.out(Reset_out[3]));
  assign not_1_out = ~u_portao_hex0;  // Not not_1, 7 bits wide
  LED Porta_Aberta (.in(u_portao_ledr[0]));
  LED Porta_Fechada (.in(u_portao_ledr[1]));
  LED Em_movimento (.in(u_portao_ledr[2]));
  Seven_Seg seven_seg_1 (
    .a(not_1_out[0]), .b(not_1_out[1]), .c(not_1_out[2]), .d(not_1_out[3]), .e(not_1_out[4]),
    .f(not_1_out[5]), .g(not_1_out[6]), .dp(1'b0));
endmodule
