// Digital circuit separados.dig as structural Verilog
module separados (
  input  S_erro,
  input  \botão ,
  input  clk
);

  wire u_sensores_abre, u_sensores_fecha, u_sensores_sout;
  wire [0:0] \Botão_out ;
  wire [6:0] not_1_out, u_motor_hex0;
  wire [9:0] u_motor_ledr;

  Button \u_Botão  (.out(\Botão_out [0]));
  LED Aberto (.in(u_motor_ledr[0]));
  LED Fechado (.in(u_motor_ledr[1]));
  sensores #(.applicationType("GHDL"), .CodeFile("C:\\Users\\Pichau\\Documents\\C0de\\UFFS\\Sistemas\\Sistemas_2\\portao\\sensores.vhd")) u_sensores (
    .sw({{7{1'b0}}, S_erro, 2'b00}), .key({clk, 2'b00, \Botão_out [0]}), .SA(u_motor_ledr[0]),
    .SF(u_motor_ledr[1]), .Fecha(u_sensores_fecha), .Abre(u_sensores_abre), .Sout(u_sensores_sout));
  Button Clock ();  // open: out
  motor #(.applicationType("GHDL"), .CodeFile("C:\\Users\\Pichau\\Documents\\C0de\\UFFS\\Sistemas\\Sistemas_2\\portao\\motor.vhd")) u_motor (
    .Fecha(u_sensores_fecha), .Abre(u_sensores_abre), .S(u_sensores_sout), .clock(clk), .ledr(u_motor_ledr),
    .hex0(u_motor_hex0));
  assign not_1_out = ~u_motor_hex0;  // Not not_1, 7 bits wide
  LED led_1 (.in(u_motor_ledr[2]));
  Seven_Seg seven_seg_1 (
    .a(not_1_out[0]), .b(not_1_out[1]), .c(not_1_out[2]), .d(not_1_out[3]), .e(not_1_out[4]),
    .f(not_1_out[5]), .g(not_1_out[6]), .dp(1'b0));
endmodule
