// Digital circuit Ex2.dig as structural Verilog
module Ex2 (
  input  [3:0] A,
  input  [3:0] B,
  input  [3:0] C,
  input  [3:0] D,
  output [3:0] S
);

  ou_vec #(.applicationType("GHDL"), .CodeFile("/home/aluno/Documentos/VHDL/Ex2.vhdl")) u_ou_vec (
    .a(A), .b(B), .c(C), .d(D), .s(S));
endmodule

/* Test case:
A B C D S
0x1 0x0 0x1 0x0 0x1
0x3 0x2 0x0 0x0 0x3
0x8 0x0 0x0 0x4 0xC
0x1 0x2 0x4 0x8 0xF
0x0 0x0 0x0 0x0 0x0
*/
