// Digital circuit 1.dig as structural Verilog
module _1 (
  input  A,
  input  B,
  input  C,
  output D,
  output E,
  output F
);

  ou #(.applicationType("GHDL"), .CodeFile("/home/aluno/Documentos/VHDL/Ex3/1.vhdl")) u_ou (
    .a(A), .b(B), .c(C), .e(D), .f(E), .d(F));
endmodule

/* Test case:
A B C D E F
0 0 0 1 1 1
0 0 1 0 1 1
0 1 0 1 1 1
0 1 1 1 1 1
1 0 0 1 1 1
1 0 1 0 1 1
1 1 0 0 1 1
1 1 1 0 1 1
*/
